# Fritzing sketch Arduino Counter (saved by Fritzing 0.9.3b)
breadboards: 1

parts:
  Part1 = Arduino Uno (Rev3)
  LCD1 = LCD screen
  R1 = Trimmer Potentiometer [maximum_resistance=10kΩ package=THT]
  VCC1 = Battery block 9V  # not connected

nets:
  N1: Part1.D8, LCD1.DB6
  N2: Part1.D9_PWM, LCD1.DB5
  N3: Part1.D10_PWM/SS, LCD1.DB4
  N4: Part1.D11_PWM/MOSI, LCD1.E
  N5: Part1.D12/MISO, LCD1.RS
  5V: Part1.5V, LCD1.VDD, LCD1.LED+, R1.leg2
  GND: Part1.GND, LCD1.VSS, LCD1.R/W, LCD1.LED-, R1.leg1
