# Fritzing sketch Arduino_BT_Vioce_LEDs_Control (saved by Fritzing 0.9.3b)
breadboards: 1

parts:
  Part1 = Bluetooth HC-05 Macho
  Part2 = Arduino Uno (Rev3)
  LED1 = smd LED [color="Red (633nm)" package="1206 [SMD]"]
  R1 = Resistor [tolerance=±5% resistance=220 package=THT]
  LED2 = smd LED [color="Red (633nm)" package="1206 [SMD]"]
  R2 = Resistor [tolerance=±5% resistance=220 package=THT]
  VCC1 = Battery block 9V

nets:
  N1: Part1.TXD, Part2.D0/RX
  N2: Part1.RXD, Part2.D1/TX
  VCC: Part1.VCC, Part2.5V
  GND: Part1.GND, Part2.GND, LED1.cathode, LED2.cathode, VCC1.-
  N3: Part2.D9_PWM, R1.Pin_1
  N4: Part2.D10_PWM/SS, R2.Pin_1
  N5: Part2.VIN, VCC1.+
  N6: LED1.anode, R1.Pin_0
  N7: LED2.anode, R2.Pin_0
