# Fritzing sketch Proximity Alarm System 1 (saved by Fritzing 0.9.3b)
breadboards: 1

parts:
  Q1 = NPN-Transistor [package="TO92 [THT]"]
  R1 = Resistor [tolerance=±5% resistance=220 package=THT]
  J1 = Piezo Speaker
  VCC1 = Battery block 9V
  Part1 = Arduino Uno (Rev3)
  hc-sr1 = hc-sr04

nets:
  GND: Q1.E, VCC1.-, Part1.GND, hc-sr1.GND
  N1: Q1.B, Part1.D3_PWM
  N2: Q1.C, J1.pin1
  N3: R1.Pin_0, J1.pin2
  5V: R1.Pin_1, VCC1.+, Part1.5V, hc-sr1.VCC
  N4: Part1.D6_PWM, hc-sr1.Echo
  N5: Part1.D7, hc-sr1.Trig
