# Fritzing sketch Proximity_Alarm_system_2 (saved by Fritzing 0.9.3b)
breadboards: 1

parts:
  Part2 = Arduino Uno (Rev3)
  Q2 = NPN-Transistor [package="TO92 [THT]"]
  R2 = Resistor [tolerance=±5% resistance=220 package=THT]
  J2 = Piezo Speaker
  VCC2 = Battery block 9V
  PIR1 = PIR sensor

nets:
  N1: Part2.D8, Q2.B
  N2: Part2.D3_PWM, PIR1.SIG
  GND: Part2.GND, Q2.E, VCC2.-, PIR1.GND
  VIN: Part2.VIN, R2.Pin_1, VCC2.+, PIR1.VDD
  N3: Q2.C, J2.pin1
  N4: R2.Pin_0, J2.pin2
