# Fritzing sketch Smart Dust Bins (saved by Fritzing 0.9.3b)
breadboards: 1

parts:
  HC-SR04_Sensor_1 = HC-SR04 Ultrasonic Distance Sensor
  J1 = Basic Servo
  Part1 = Arduino Uno (Rev3)

nets:
  VCC: HC-SR04_Sensor_1.VCC, J1.vcc, Part1.5V
  N1: HC-SR04_Sensor_1.TRIG, Part1.D11_PWM/MOSI
  N2: HC-SR04_Sensor_1.ECHO, Part1.D10_PWM/SS
  GND: HC-SR04_Sensor_1.GND, J1.gnd, Part1.GND
  N3: J1.pulse, Part1.D5_PWM
